// Logisim project cpu.circ as structural Verilog: 7 circuits, main circuit main
module PC (
  input  [23:0] Bdst,
  input  Br,
  output [31:0] Instr
);

  wire CLK;
  wire [23:0] adder_1_out, nextPC, PC;

  Clock clock_1 (.out(CLK));
  Register #(.width(24)) register_1 (.D(nextPC), .en(1'b1), .clk(CLK), .Q(PC));  // open: clr
  Adder #(.width(24)) adder_1 (.a(PC), .b(24'h1), .out(adder_1_out));  // open: cin, cout
  RAM #(.addrWidth(24), .dataWidth(32), .enables("line")) Instruction_Memory (
    .addr(PC), .we(1'b0), .clk(CLK), .dout(Instr));  // open: din
  Multiplexer #(.width(24)) multiplexer_1 (.in0(adder_1_out), .in1(Bdst), .out(nextPC), .sel(Br));
endmodule

module main (
  output [31:0] RegDataW
);

  wire Br, ControlUnit_1_p3, ControlUnit_1_p4, ControlUnit_1_p6, ControlUnit_1_p9, ControlUnit_1_p12,
       MemRead, MemToReg, MemWrite, RegWrite;
  wire [3:0] ALUop;
  wire [4:0] LinkReg, ReadReg1, ReadReg2, ReadReg3, WriteReg;
  wire [23:0] Bdst;
  wire [31:0] ALUout, Instr, ReadDataM, RegData1, Regdata1_t, RegData2, Regdata2_t, RegData3, Regdata3_t,
       RegDataW_t, WriteDataM;

  Multiplexer #(.width(32)) multiplexer_1 (.in0(ALUout), .in1(ReadDataM), .out(RegDataW), .sel(MemToReg));
  PC PC_1 (.Bdst(Bdst), .Br(Br), .Instr(Instr));
  // ControlUnit ControlUnit_1: pin names not known; wires that end beside it: Instr, WriteDataM, ControlUnit_1_p3, ControlUnit_1_p4, ReadReg1, ControlUnit_1_p6, ReadReg2, MemToReg, ControlUnit_1_p9, MemWrite, LinkReg, ControlUnit_1_p12, Br
  RegFile RegFile_1 (
    .RegDataW(RegDataW_t), .RegWrite(RegWrite), .WriteReg(WriteReg), .ReadReg1(ReadReg1),
    .ReadReg2(ReadReg2), .ReadReg3(ReadReg3), .RegData1(RegData1), .RegData2(RegData2), .RegData3(RegData3));
  ALU ALU_1 (
    .RegData1(Regdata1_t), .RegData2(Regdata2_t), .RegData3(Regdata3_t), .MemWrite(MemWrite),
    .MemRead(MemRead), .ALUop(ALUop), .Bdst(Bdst), .ALUout(ALUout));
  MEM MEM_1 (.MemRead(MemRead), .MemWrite(MemWrite), .WriteDataM(WriteDataM), .ALUout(ALUout), .ReadDataM(ReadDataM));

  // Notes on the sheet:
  //   Stage 1: IF
  //   Stage 2: ID
  //   Stage 3: EX
  //   Stage 4: ME
  //   Stage 5: WB
endmodule

module RegFile (
  input  [31:0] RegDataW,
  input  RegWrite,
  input  [4:0] WriteReg,
  input  [4:0] ReadReg1,
  input  [4:0] ReadReg2,
  input  [4:0] ReadReg3,
  output [31:0] RegData1,
  output [31:0] RegData2,
  output [31:0] RegData3
);

  wire CLK, WE0, WE1, WE2, WE3, WE4, WE5, WE6, WE7, WE8, WE9, WE10, WE11, WE12, WE13, WE14, WE15, WE16, WE17,
       WE18, WE19, WE20, WE21, WE22, WE23, WE24, WE25, WE26, WE27, WE28, WE29, WE30, WE31, WR0, WR1, WR2,
       WR3, WR4, WR5, WR6, WR7, WR8, WR9, WR10, WR11, WR12, WR13, WR14, WR15, WR16, WR17, WR18, WR19, WR20,
       WR21, WR22, WR23, WR24, WR25, WR26, WR27, WR28, WR29, WR30, WR31;
  wire [31:0] R0d, R1d, R2d, R3d, R4d, R5d, R6d, R7d, R8d, R9d, R10d, R11d, R12d, R13d, R14d, R15d, R16d,
       R17d, R18d, R19d, R20d, R21d, R22d, R23d, R24d, R25d, R26d, R27d, R28d, R29d, R30d, R31d;

  Decoder #(.select(5)) decoder_1 (
    .out0(WR0), .out1(WR1), .out2(WR2), .out3(WR3), .out4(WR4), .out5(WR5), .out6(WR6), .out7(WR7),
    .out8(WR8), .out9(WR9), .out10(WR10), .out11(WR11), .out12(WR12), .out13(WR13), .out14(WR14),
    .out15(WR15), .out16(WR16), .out17(WR17), .out18(WR18), .out19(WR19), .out20(WR20), .out21(WR21),
    .out22(WR22), .out23(WR23), .out24(WR24), .out25(WR25), .out26(WR26), .out27(WR27), .out28(WR28),
    .out29(WR29), .out30(WR30), .out31(WR31), .sel(WriteReg));  // open: en
  Clock clock_1 (.out(CLK));
  and and_1 (WE0, RegWrite, WR0);
  and and_2 (WE1, RegWrite, WR1);
  and and_3 (WE2, RegWrite, WR2);
  and and_4 (WE3, RegWrite, WR3);
  and and_5 (WE4, RegWrite, WR4);
  and and_6 (WE5, RegWrite, WR5);
  and and_7 (WE6, RegWrite, WR6);
  and and_8 (WE7, RegWrite, WR7);
  and and_9 (WE8, RegWrite, WR8);
  and and_10 (WE9, RegWrite, WR9);
  and and_11 (WE10, RegWrite, WR10);
  and and_12 (WE11, RegWrite, WR11);
  and and_13 (WE12, RegWrite, WR12);
  and and_14 (WE13, RegWrite, WR13);
  and and_15 (WE14, RegWrite, WR14);
  and and_16 (WE15, RegWrite, WR15);
  and and_17 (WE16, RegWrite, WR16);
  and and_18 (WE17, RegWrite, WR17);
  and and_19 (WE18, RegWrite, WR18);
  and and_20 (WE19, RegWrite, WR19);
  and and_21 (WE20, RegWrite, WR20);
  and and_22 (WE21, RegWrite, WR21);
  and and_23 (WE22, RegWrite, WR22);
  and and_24 (WE23, RegWrite, WR23);
  and and_25 (WE24, RegWrite, WR24);
  and and_26 (WE25, RegWrite, WR25);
  and and_27 (WE26, RegWrite, WR26);
  and and_28 (WR27, RegWrite, WR27);
  and and_29 (WR28, RegWrite, WR28);
  and and_30 (WR29, RegWrite, WR29);
  and and_31 (WE30, RegWrite, WR30);
  and and_32 (WE31, RegWrite, WR31);
  Register #(.width(32)) R0 (.D({32{1'b0}}), .en(WE0), .clk(CLK), .Q(R0d));  // open: clr
  Register #(.width(32)) R1 (.D(RegDataW), .en(WE1), .clk(CLK), .Q(R1d));  // open: clr
  Register #(.width(32)) R2 (.D(RegDataW), .en(WE2), .clk(CLK), .Q(R2d));  // open: clr
  Register #(.width(32)) R3 (.D(RegDataW), .en(WE3), .clk(CLK), .Q(R3d));  // open: clr
  Register #(.width(32)) R4 (.D(RegDataW), .en(WE4), .clk(CLK), .Q(R4d));  // open: clr
  Register #(.width(32)) R5 (.D(RegDataW), .en(WE5), .clk(CLK), .Q(R5d));  // open: clr
  Register #(.width(32)) R6 (.D(RegDataW), .en(WE6), .clk(CLK), .Q(R6d));  // open: clr
  Register #(.width(32)) R7 (.D(RegDataW), .en(WE7), .clk(CLK), .Q(R7d));  // open: clr
  Multiplexer #(.select(5), .width(32)) multiplexer_1 (
    .in0(R0d), .in1(R1d), .in2(R2d), .in3(R3d), .in4(R4d), .in5(R5d), .in6(R6d), .in7(R7d), .in8(R8d),
    .in9(R9d), .in10(R10d), .in11(R11d), .in12(R12d), .in13(R13d), .in14(R14d), .in15(R15d), .in16(R16d),
    .in17(R17d), .in18(R18d), .in19(R19d), .in20(R20d), .in21(R21d), .in22(R22d), .in23(R23d), .in24(R24d),
    .in25(R25d), .in26(R26d), .in27(R27d), .in28(R28d), .in29(R29d), .in30(R30d), .in31(R31d),
    .out(RegData1), .sel(ReadReg1));
  Register #(.width(32)) R8 (.D(RegDataW), .en(WE8), .clk(CLK), .Q(R8d));  // open: clr
  Register #(.width(32)) R9 (.D(RegDataW), .en(WE9), .clk(CLK), .Q(R9d));  // open: clr
  Register #(.width(32)) R10 (.D(RegDataW), .en(WE10), .clk(CLK), .Q(R10d));  // open: clr
  Register #(.width(32)) R11 (.D(RegDataW), .en(WE11), .clk(CLK), .Q(R11d));  // open: clr
  Register #(.width(32)) R12 (.D(RegDataW), .en(WE12), .clk(CLK), .Q(R12d));  // open: clr
  Register #(.width(32)) R13 (.D(RegDataW), .en(WE13), .clk(CLK), .Q(R13d));  // open: clr
  Register #(.width(32)) R14 (.D(RegDataW), .en(WE14), .clk(CLK), .Q(R14d));  // open: clr
  Register #(.width(32)) R15 (.D(RegDataW), .en(WE15), .clk(CLK), .Q(R15d));  // open: clr
  Multiplexer #(.select(5), .width(32)) multiplexer_2 (
    .in0(R0d), .in1(R1d), .in2(R2d), .in3(R3d), .in4(R4d), .in5(R5d), .in6(R6d), .in7(R7d), .in8(R8d),
    .in9(R9d), .in10(R10d), .in11(R11d), .in12(R12d), .in13(R13d), .in14(R14d), .in15(R15d), .in16(R16d),
    .in17(R17d), .in18(R18d), .in19(R19d), .in20(R20d), .in21(R21d), .in22(R22d), .in23(R23d), .in24(R24d),
    .in25(R25d), .in26(R26d), .in27(R27d), .in28(R28d), .in29(R29d), .in30(R30d), .in31(R31d),
    .out(RegData3), .sel(ReadReg3));
  Register #(.width(32)) R16 (.D(RegDataW), .en(WE16), .clk(CLK), .Q(R16d));  // open: clr
  Register #(.width(32)) R17 (.D(RegDataW), .en(WE17), .clk(CLK), .Q(R17d));  // open: clr
  Register #(.width(32)) R18 (.D(RegDataW), .en(WE18), .clk(CLK), .Q(R18d));  // open: clr
  Register #(.width(32)) R19 (.D(RegDataW), .en(WE19), .clk(CLK), .Q(R19d));  // open: clr
  Register #(.width(32)) R20 (.D(RegDataW), .en(WE20), .clk(CLK), .Q(R20d));  // open: clr
  Register #(.width(32)) R21 (.D(RegDataW), .en(WE21), .clk(CLK), .Q(R21d));  // open: clr
  Register #(.width(32)) R22 (.D(RegDataW), .en(WE22), .clk(CLK), .Q(R22d));  // open: clr
  Register #(.width(32)) R23 (.D(RegDataW), .en(WE23), .clk(CLK), .Q(R23d));  // open: clr
  Multiplexer #(.select(5), .width(32)) multiplexer_3 (
    .in0(R0d), .in1(R1d), .in2(R2d), .in3(R3d), .in4(R4d), .in5(R5d), .in6(R6d), .in7(R7d), .in8(R8d),
    .in9(R9d), .in10(R10d), .in11(R11d), .in12(R12d), .in13(R13d), .in14(R14d), .in15(R15d), .in16(R16d),
    .in17(R17d), .in18(R18d), .in19(R19d), .in20(R20d), .in21(R21d), .in22(R22d), .in23(R23d), .in24(R24d),
    .in25(R25d), .in26(R26d), .in27(R27d), .in28(R28d), .in29(R29d), .in30(R30d), .in31(R31d),
    .out(RegData2), .sel(ReadReg2));
  Register #(.width(32)) R24 (.D(RegDataW), .en(WE24), .clk(CLK), .Q(R24d));  // open: clr
  Register #(.width(32)) R25 (.D(RegDataW), .en(WE25), .clk(CLK), .Q(R25d));  // open: clr
  Register #(.width(32)) R26 (.D(RegDataW), .en(WE26), .clk(CLK), .Q(R26d));  // open: clr
  Register #(.width(32)) R27 (.D(RegDataW), .en(WE27), .clk(CLK), .Q(R27d));  // open: clr
  Register #(.width(32)) R28 (.D(RegDataW), .en(WE28), .clk(CLK), .Q(R28d));  // open: clr
  Register #(.width(32)) R29 (.D(RegDataW), .en(WE29), .clk(CLK), .Q(R29d));  // open: clr
  Register #(.width(32)) R30_CMP (.D(RegDataW), .en(WE30), .clk(CLK), .Q(R30d));  // open: clr
  Register #(.width(32)) R31_LR (.D(RegDataW), .en(WE31), .clk(CLK), .Q(R31d));  // open: clr
endmodule

module ALU (
  input  [31:0] RegData1,
  input  [31:0] RegData2,
  input  [31:0] RegData3,
  input  MemWrite,
  input  MemRead,
  input  [3:0] ALUop,
  output [23:0] Bdst,
  output [31:0] ALUout
);

  wire [31:0] adder_1_out, and_1_out, divider_1_out, multiplier_1_out, negator_1_out, or_1_out, RegData2_t,
       shifter_1_out, shifter_2_out, shifter_3_out, subtractor_1_out, xor_1_out;

  Adder #(.width(32)) adder_1 (.a(RegData1), .b(RegData2_t), .out(adder_1_out));  // open: cin, cout
  Subtractor #(.width(32)) subtractor_1 (.a(RegData1), .b(RegData2_t), .out(subtractor_1_out));  // open: bin, bout
  Multiplier #(.width(32)) multiplier_1 (.a(RegData1), .b(RegData2_t), .out(multiplier_1_out));  // open: cin, cout
  Divider #(.width(32)) divider_1 (.a(RegData1), .b(RegData2_t), .out(divider_1_out));  // open: upper, rem
  assign and_1_out = RegData1 & RegData2_t;  // AND_Gate and_1, 32 bits wide
  assign or_1_out = RegData1 | RegData2_t;  // OR_Gate or_1, 32 bits wide
  assign xor_1_out = RegData1 ^ RegData2_t;  // XOR_Gate xor_1, 32 bits wide
  Shifter #(.width(32)) shifter_1 (.in(RegData1), .\dist (RegData2_t[4:0]), .out(shifter_1_out));
  Shifter #(.shift("lr"), .width(32)) shifter_2 (.in(RegData1), .\dist (RegData2_t[4:0]), .out(shifter_2_out));
  Shifter #(.shift("ar"), .width(32)) shifter_3 (.in(RegData1), .\dist (RegData2_t[4:0]), .out(shifter_3_out));
  Negator #(.width(32)) negator_1 (.in(RegData1), .out(negator_1_out));
  Multiplexer #(.select(4), .width(32)) multiplexer_1 (
    .in0(adder_1_out), .in1(subtractor_1_out), .in2(multiplier_1_out), .in3(divider_1_out), .in4(and_1_out),
    .in5(or_1_out), .in6(xor_1_out), .in7(shifter_1_out), .in8(shifter_2_out), .in9(shifter_3_out),
    .in10(negator_1_out), .out(ALUout), .sel(ALUop));  // open: in11, in12, in13, in14, in15

  assign RegData2 = RegData1;
  assign RegData3 = RegData1;

  // Notes on the sheet:
  //   0000 - ADD
  //   0001 - SUB
  //   0010 - MUL
  //   0011 - DIV
  //   0100 - AND
  //   0101 - ORR
  //   0110 - XOR
  //   0111 - LSL
  //   1000 - LSR
  //   1001 - ASR
  //   1010 - NEG
endmodule

module ControlUnit (
  input  [31:0] Instr,
  output [31:0] WriteDataM,
  output ALUsrc,
  output [4:0] ReadReg1,
  output MemRead,
  output [4:0] ReadReg2,
  output MemToReg,
  output [4:0] ReadReg3,
  output [4:0] WriteReg,
  output ALUop,
  output MemWrite,
  output LinkReg,
  output Br,
  output RegWrite
);

  wire A_N_D, ADD, ADR, ASR, B, BEQ, BGE, BGT, BLE, BLT, BNE, CBNZ, CBZ, DIV, LDR, LSL, LSR, MUL, NEG, ORR,
       RET, SUB, X_O_R;

  Comparator #(.width(6)) comparator_1 (.a(Instr[31:26]), .b(6'b100000), .eq(B));  // open: gt, lt
  Comparator #(.width(6)) comparator_2 (.a(Instr[31:26]), .b(6'b100001), .eq(LinkReg));  // open: gt, lt
  Comparator #(.width(6)) comparator_3 (.a(Instr[31:26]), .b(6'b100010), .eq(BEQ));  // open: gt, lt
  Comparator #(.width(6)) comparator_4 (.a(Instr[31:26]), .b(6'b100011), .eq(BNE));  // open: gt, lt
  Comparator #(.width(6)) comparator_5 (.a(Instr[31:26]), .b(6'b100100), .eq(BGT));  // open: gt, lt
  Comparator #(.width(6)) comparator_6 (.a(Instr[31:26]), .b(6'b100101), .eq(BLT));  // open: gt, lt
  Comparator #(.width(6)) comparator_7 (.a(Instr[31:26]), .b(6'b100110), .eq(BGE));  // open: gt, lt
  Comparator #(.width(6)) comparator_8 (.a(Instr[31:26]), .b(6'b100111), .eq(BLE));  // open: gt, lt
  Comparator #(.width(6)) comparator_9 (.a(Instr[31:26]), .b(6'b110101), .eq(CBZ));  // open: gt, lt
  Comparator #(.width(6)) comparator_10 (.a(Instr[31:26]), .b(6'b110110), .eq(CBNZ));  // open: gt, lt
  Comparator #(.width(6)) comparator_11 (.a(Instr[31:26]), .b(6'b110001), .eq(RET));  // open: gt, lt
  Comparator #(.width(6)) comparator_12 (.a(Instr[31:26]), .b({6{1'b0}}), .eq(ADD));  // open: gt, lt
  Comparator #(.width(6)) comparator_13 (.a(Instr[31:26]), .b(6'b000001), .eq(SUB));  // open: gt, lt
  Comparator #(.width(6)) comparator_14 (.a(Instr[31:26]), .b(6'b000010), .eq(MUL));  // open: gt, lt
  Comparator #(.width(6)) comparator_15 (.a(Instr[31:26]), .b(6'b000011), .eq(DIV));  // open: gt, lt
  Comparator #(.width(6)) comparator_16 (.a(Instr[31:26]), .b(6'b000100), .eq(A_N_D));  // open: gt, lt
  Comparator #(.width(6)) comparator_17 (.a(Instr[31:26]), .b(6'b000101), .eq(ORR));  // open: gt, lt
  Comparator #(.width(6)) comparator_18 (.a(Instr[31:26]), .b(6'b000110), .eq(X_O_R));  // open: gt, lt
  Comparator #(.width(6)) comparator_19 (.a(Instr[31:26]), .b(6'b000111), .eq(LSL));  // open: gt, lt
  Comparator #(.width(6)) comparator_20 (.a(Instr[31:26]), .b(6'b001000), .eq(LSR));  // open: gt, lt
  Comparator #(.width(6)) comparator_21 (.a(Instr[31:26]), .b(6'b001001), .eq(ASR));  // open: gt, lt
  Comparator #(.width(6)) comparator_22 (.a(Instr[31:26]), .b(6'b001010), .eq(NEG));  // open: gt, lt
  Comparator #(.width(6)) comparator_23 (.a(Instr[31:26]), .b(6'b010000), .eq(LDR));  // open: gt, lt
  Comparator #(.width(6)) comparator_24 (.a(Instr[31:26]), .b(6'b010010), .eq(ADR));  // open: gt, lt
  Comparator #(.width(6)) comparator_25 (.a(Instr[31:26]), .b(6'b010000), .eq(MemRead));  // open: gt, lt
  Comparator #(.width(6)) comparator_26 (.a(Instr[31:26]), .b(6'b010001), .eq(MemWrite));  // open: gt, lt
  or or_1 (RegWrite, ADD, SUB, MUL, DIV, A_N_D, ORR, X_O_R, LSL, LSR, ASR, NEG, LDR, ADR);
  or or_2 (Br, B, LinkReg, BEQ, BNE, BGT, BLT, BGE, BLE, CBZ, CBNZ);

  assign ALUsrc = Instr[25];
  assign MemToReg = MemRead;
  assign ReadReg1 = {5{1'b1}};
  assign ReadReg2 = {5{1'b1}};
  assign ReadReg3 = {5{1'b1}};
  assign WriteReg = {5{1'b1}};

  // Other names for the same wires on the sheet: BL = LinkReg; opcode[5:0] = Instr[31:26]; Rd[4:0] = Instr[24:20];
  //   Rm[4:0] = Instr[14:10]; Rn[4:0] = Instr[19:15]

  // Notes on the sheet:
  //   Opcode
  //   LDR
  //   STR
  //   Instr w/o Opcode
endmodule

module MEM (
  input  MemRead,
  input  MemWrite,
  input  [31:0] WriteDataM,
  input  [31:0] ALUout,
  output [31:0] ReadDataM
);

  wire CLK;
  wire [23:0] bit_extender_1_out;

  Clock clock_1 (.out(CLK));
  Bit_Extender #(.in_width(32), .out_width(24)) bit_extender_1 (.in(ALUout), .out(bit_extender_1_out));
  RAM #(.addrWidth(24), .dataWidth(32), .enables("line")) DRAM (
    .addr(bit_extender_1_out), .we(MemRead), .clk(CLK), .din(WriteDataM), .dout(ReadDataM));
endmodule

module cache (
  input  [23:0] Address,
  input  [31:0] DataIn,
  output [31:0] DataOut
);

  wire and_1_out, CLK, comparator_1_eq, Miss, ValidBit;
  wire [15:0] StoredTag;
  wire [31:0] CacheData;

  Clock clock_1 (.out(CLK));
  RAM #(.dataWidth(16), .enables("line")) TagMemory (
    .addr(Address[7:0]), .we(Miss), .clk(CLK), .din(Address[23:8]), .dout(StoredTag));
  RAM #(.dataWidth(1), .enables("line")) ValidBitMemory (
    .addr(Address[7:0]), .we(Miss), .clk(CLK), .din(1'b1), .dout(ValidBit));
  Comparator #(.width(16)) comparator_1 (.a(Address[23:8]), .b(StoredTag), .eq(comparator_1_eq));  // open: gt, lt
  and and_1 (and_1_out, comparator_1_eq, ValidBit);
  Multiplexer #(.width(32)) multiplexer_1 (.in0(DataIn), .in1(CacheData), .out(DataOut), .sel(and_1_out));
  not not_1 (Miss, and_1_out);
  RAM #(.dataWidth(32), .enables("line")) DataMemory (
    .addr(Address[7:0]), .we(Miss), .clk(CLK), .din(DataIn), .dout(CacheData));

  // Other names for the same wires on the sheet: Index[7:0] = Address[7:0]; Tag[15:0] = Address[23:8]
endmodule
